# Fritzing sketch Cableado_Power_Switchable (saved by Fritzing 0.8.7b)
breadboards: 1

parts:
  Parte1 = Arduino Uno (Rev3)
  DFRobot_Bluetooth_V1 = TEL0026-BluetoothV3
  IC1 = IC, DIP package, 16 pins [chip_label=L293D]
  R1 = Resistor [tolerance=±5% resistance=10k package=THT]
  R2 = Photocell (LDR) [package=THT]

nets:
  N1: Parte1.A0, R1.Pin_1, R2.pin_0
  N2: Parte1.D8, IC1.pin1
  N3: Parte1.D3_PWM, DFRobot_Bluetooth_V1.RXD
  N4: Parte1.5V, IC1.pin2, IC1.pin8, IC1.pin16, R1.Pin_0
  N5: Parte1.GND, DFRobot_Bluetooth_V1.GND#connector1pad-4-5-0-3-1-0, IC1.pin4, R2.pin_1
  N6: DFRobot_Bluetooth_V1.VCC, IC1.pin3
