# Fritzing sketch Cableado_MEGA (saved by Fritzing 0.8.7b)

parts:
  DFRobot_Bluetooth_V1 = TEL0026-BluetoothV3
  Parte1 = Arduino Mega 2560 (Rev3)

nets:
  N1: DFRobot_Bluetooth_V1.TXD, Parte1.D19/RX1
  VCC: DFRobot_Bluetooth_V1.VCC, Parte1.5V
  GND: DFRobot_Bluetooth_V1.GND, Parte1.GND
  N2: DFRobot_Bluetooth_V1.RXD, Parte1.D18/TX1
