# Fritzing sketch Cableado_MEGA_buffer (saved by Fritzing 0.8.7b)
breadboards: 1

parts:
  DFRobot_Bluetooth_V2 = TEL0026-BluetoothV3
  IC2 = L293D [package=THT]
  Parte3 = Arduino Mega 2560 (Rev3)

nets:
  N1: DFRobot_Bluetooth_V2.TXD, Parte3.D19/RX1
  N2: DFRobot_Bluetooth_V2.VCC, IC2.Out_3_(_Controlled_by_Enable_2_)
  N3: DFRobot_Bluetooth_V2.GND#connector1pad-4-5-0-3-1-0, IC2.0V, Parte3.GND
  N4: DFRobot_Bluetooth_V2.RXD, Parte3.D3_PWM
  N5: IC2.+Vmotor, IC2.In_3, IC2.+V, Parte3.5V
  N6: IC2.Enable_2, Parte3.D18/TX1
