# Fritzing sketch Cableado_UNO (saved by Fritzing 0.8.7b)

parts:
  Parte1 = Arduino Uno (Rev3)
  DFRobot_Bluetooth_V1 = TEL0026-BluetoothV3

nets:
  GND: Parte1.GND, DFRobot_Bluetooth_V1.GND
  N1: Parte1.D2, DFRobot_Bluetooth_V1.TXD
  N2: Parte1.D3_PWM, DFRobot_Bluetooth_V1.RXD
  5V: Parte1.5V, DFRobot_Bluetooth_V1.VCC
