# Fritzing sketch Cableado_UNO_buffer (saved by Fritzing 0.8.7b)
breadboards: 1

parts:
  Parte1 = Arduino Uno (Rev3)
  DFRobot_Bluetooth_V1 = TEL0026-BluetoothV3
  IC1 = L293D [package=THT]

nets:
  N1: Parte1.D8, IC1.Enable_2
  N2: Parte1.GND, DFRobot_Bluetooth_V1.GND#connector1pad-4-5-0-3-1-0, IC1.0V
  N3: Parte1.D2, DFRobot_Bluetooth_V1.TXD
  N4: Parte1.D3_PWM, DFRobot_Bluetooth_V1.RXD
  N5: DFRobot_Bluetooth_V1.VCC, IC1.Out_3_(_Controlled_by_Enable_2_)
  N6: IC1.+Vmotor, IC1.In_3, IC1.+V
