# Fritzing sketch Esquema-Prototipo_BT (saved by Fritzing 0.8.7b)
breadboards: 1

parts:
  Parte1 = Arduino Uno (Rev3)
  R2 = Photocell (LDR) [package=THT]
  R3 = Resistor [tolerance=±5% resistance=10k package=THT]
  DFRobot_Bluetooth_V1 = TEL0026-BluetoothV3
  R1 = Resistor [tolerance=±5% resistance=220 package=THT]
  LED1 = LED - 5mm [color="Green (555nm)" package="5 mm [THT]"]

nets:
  N1: Parte1.A0, R2.pin_1, R3.Pin_0
  N2: Parte1.D10_PWM/SS, LED1.cathode
  N3: Parte1.GND, R2.pin_0, DFRobot_Bluetooth_V1.GND#connector1pad-4-5-0-3-1-0
  N4: Parte1.D2, DFRobot_Bluetooth_V1.GND#connector1pad-4-2-34-77
  N5: Parte1.D3_PWM, DFRobot_Bluetooth_V1.TXD
  5V: Parte1.5V, R3.Pin_1, DFRobot_Bluetooth_V1.VCC, R1.Pin_1
  N6: R1.Pin_0, LED1.anode
